// Logisim project lab7part2.circ as structural Verilog
module ParityGen (
  input  [3:0] \input ,
  input  in_2,
  output X2,
  output X1,
  output X0
);

  wire and_1_out, and_2_out, and_3_out, and_4_out, and_5_out, and_6_out, and_7_out, not_1_out, not_2_out,
       not_3_out, not_4_out, not_5_out, or_1_out, or_2_out, or_3_out, xor_1_out, xor_2_out;

  not not_1 (not_1_out, \input [2]);
  not not_2 (not_2_out, \input [1]);
  not not_3 (not_3_out, \input [0]);
  not not_4 (not_4_out, \input [1]);
  not not_5 (not_5_out, \input [3]);
  or or_1 (or_1_out, \input [1], \input [0]);
  or or_2 (or_2_out, \input [2], \input [3]);
  xor xor_1 (xor_1_out, \input [0], \input [3]);
  xor xor_2 (xor_2_out, \input [2], \input [3]);
  and and_1 (and_1_out, \input [2], not_4_out);
  and and_2 (and_2_out, \input [1], not_5_out);
  and and_3 (and_3_out, \input [3], \input [2], or_1_out);
  and and_4 (and_4_out, \input [0], \input [1], or_2_out);
  and and_5 (and_5_out, xor_1_out, not_1_out);
  and and_6 (and_6_out, xor_2_out, not_2_out);
  and and_7 (and_7_out, not_3_out, or_3_out);
  or or_3 (or_3_out, and_1_out, and_2_out);
  or or_4 (X2, and_3_out, and_4_out);
  or or_5 (X1, and_5_out, and_6_out, and_7_out);

  assign X0 = in_2;
endmodule
