// Logisim project lab8part1.circ as structural Verilog: 1 circuit, main circuit main
module main (
  input  in_1,
  input  ReadRegister1,
  input  in_3,
  input  ReadRegister2,
  input  WriteEnable,
  input  in_6,
  input  WriteRegister,
  input  [15:0] in_8,
  output [15:0] out_9,
  output [15:0] out_10
);

  wire clock_1_out, demultiplexer_1_out0, demultiplexer_1_out1, demultiplexer_1_out2, demultiplexer_1_out3;
  wire [15:0] register_1_q, register_2_q, register_3_q, register_4_q;

  Demultiplexer #(.select(2), .enable("false")) demultiplexer_1 (
    .out0(demultiplexer_1_out0), .out1(demultiplexer_1_out1), .out2(demultiplexer_1_out2),
    .out3(demultiplexer_1_out3), .in(WriteEnable), .sel({WriteRegister, in_6}));
  Clock clock_1 (.out(clock_1_out));
  Register #(.width(16)) register_1 (
    .D(in_8), .en(demultiplexer_1_out0), .Q(register_1_q), .clk(clock_1_out));  // open: clr
  Register #(.width(16)) register_2 (
    .D(in_8), .en(demultiplexer_1_out1), .Q(register_2_q), .clk(clock_1_out));  // open: clr
  Register #(.width(16)) register_3 (
    .D(in_8), .en(demultiplexer_1_out2), .Q(register_3_q), .clk(clock_1_out));  // open: clr
  Register #(.width(16)) register_4 (
    .D(in_8), .en(demultiplexer_1_out3), .Q(register_4_q), .clk(clock_1_out));  // open: clr
  Multiplexer #(.select(2), .width(16), .enable("false")) multiplexer_1 (
    .in0(register_1_q), .in1(register_2_q), .in2(register_3_q), .in3(register_4_q), .out(out_9),
    .sel({ReadRegister1, in_1}));
  Multiplexer #(.select(2), .width(16), .enable("false")) multiplexer_2 (
    .in0(register_1_q), .in1(register_2_q), .in2(register_3_q), .in3(register_4_q), .out(out_10),
    .sel({ReadRegister2, in_3}));

  // Notes on the sheet:
  //   WriteData
  //   ReadData1
  //   ReadData2
endmodule
