// Logisim project lab8part2.circ as structural Verilog: 1 circuit, main circuit main
module main (
  input  [7:0] Set_to_0x42
);

  wire adder_1_cout, Clock_out, multiplexer_1_out, not_1_out, Reset_out;
  wire [7:0] adder_1_out, ram_1_data, register_1_q;

  Multiplexer #(.enable("false")) multiplexer_1 (.in0(1'b1), .in1(1'b0), .out(multiplexer_1_out), .sel(adder_1_cout));
  Button Reset (.out(Reset_out));
  Clock Clock (.out(Clock_out));
  Adder adder_1 (.a(register_1_q), .b(8'h1), .out(adder_1_out), .cin(1'b0), .cout(adder_1_cout));
  Register register_1 (.D(adder_1_out), .en(multiplexer_1_out), .Q(register_1_q), .clk(Clock_out), .clr(Reset_out));
  RAM ram_1 (.addr(register_1_q), .data(ram_1_data), .clk(Clock_out), .ld(not_1_out));  // open: sel, clr
  not not_1 (not_1_out, 1'b1);
  assign ram_1_data = 1'b1 ? Set_to_0x42 : 8'bz;  // Controlled_Buffer controlled_buffer_1
endmodule
