// Logisim project CoeMIPS_wReset.circ as structural Verilog: 7 circuits, main circuit RegFile
module main (
);

  wire branch_1_branch, Clock_out, control_1_alusrc, control_1_hexw, control_1_jr, control_1_memr,
       control_1_memtoreg, control_1_memw, control_1_pctoreg, control_1_progen, control_1_regwrite,
       decoder_1_subop, not_1_out, Reset_out;
  wire [2:0] control_1_aluop, control_1_branchop, decoder_1_rs, decoder_1_rt;
  wire [3:0] decoder_1_opcode;
  wire [8:0] decoder_1_imm;
  wire [15:0] adder_1_out, alu_1_aluout, multiplexer_1_out, multiplexer_2_out, multiplexer_3_out,
       multiplexer_4_out, multiplexer_5_out, PC_q, ram_1_data, regfile_1_rs_2, regfile_1_rt_2, register_1_q,
       rom_1_data, signing_1_imm_value;

  Button Reset (.out(Reset_out));
  Clock Clock (.out(Clock_out));
  Register #(.width(16)) register_1 (
    .D(regfile_1_rs_2), .en(control_1_hexw), .Q(register_1_q), .clk(Clock_out), .clr(Reset_out));
  Hex_Digit_Display hex_digit_display_1 (.value(register_1_q[15:12]));  // open: dp
  LED led_1 (.in(not_1_out));
  Register #(.width(16)) PC (.D(multiplexer_4_out), .en(control_1_progen), .Q(PC_q), .clk(Clock_out), .clr(Reset_out));
  not not_1 (not_1_out, control_1_progen);
  Hex_Digit_Display hex_digit_display_2 (.value(register_1_q[11:8]));  // open: dp
  Hex_Digit_Display hex_digit_display_3 (.value(register_1_q[3:0]));  // open: dp
  Hex_Digit_Display hex_digit_display_4 (.value(register_1_q[7:4]));  // open: dp
  ROM #(.addrWidth(16), .dataWidth(16)) rom_1 (.addr(PC_q), .data(rom_1_data), .sel(control_1_progen));
  Decoder decoder_1 (
    .Inst(rom_1_data), .OPcode(decoder_1_opcode), .RT(decoder_1_rt), .RS(decoder_1_rs), .Imm(decoder_1_imm),
    .SubOP(decoder_1_subop));
  Adder #(.width(16)) adder_1 (.a(16'h1), .b(PC_q), .out(adder_1_out));  // open: cin, cout
  Control control_1 (
    .OP(decoder_1_opcode), .SubOP(decoder_1_subop), .RegWrite(control_1_regwrite), .ALUsrc(control_1_alusrc),
    .ALUop(control_1_aluop), .MemR(control_1_memr), .MemW(control_1_memw), .MemToReg(control_1_memtoreg),
    .PCtoReg(control_1_pctoreg), .HexW(control_1_hexw), .ProgEn(control_1_progen), .JR(control_1_jr),
    .BranchOP(control_1_branchop));
  Signing signing_1 (.Sign___Imm(decoder_1_imm), .Imm_Value(signing_1_imm_value));
  Multiplexer #(.width(16), .enable("false")) multiplexer_1 (
    .in0(adder_1_out), .in1(regfile_1_rs_2), .out(multiplexer_1_out), .sel(control_1_jr));
  RegFile regfile_1 (
    .RT(decoder_1_rt), .WriteData(multiplexer_3_out), .WriteEnable(control_1_regwrite), .RS(decoder_1_rs),
    .RT_2(regfile_1_rt_2), .RS_2(regfile_1_rs_2), .Clock(Clock_out));
  Multiplexer #(.width(16), .enable("false")) multiplexer_2 (
    .in0(regfile_1_rt_2), .in1(signing_1_imm_value), .out(multiplexer_2_out), .sel(control_1_alusrc));
  Multiplexer #(.width(16), .enable("false")) multiplexer_3 (
    .in0(multiplexer_5_out), .in1(adder_1_out), .out(multiplexer_3_out), .sel(control_1_pctoreg));
  Multiplexer #(.width(16), .enable("false")) multiplexer_4 (
    .in0(multiplexer_1_out), .in1(signing_1_imm_value), .out(multiplexer_4_out), .sel(branch_1_branch));
  Branch branch_1 (.RS(regfile_1_rs_2), .BranchOp(control_1_branchop), .Branch(branch_1_branch));
  ALU alu_1 (
    .RS(regfile_1_rs_2), .RT_IMM(multiplexer_2_out), .SUBOP(decoder_1_subop), .ALUOP(control_1_aluop),
    .ALUout(alu_1_aluout));
  RAM #(.addrWidth(16), .dataWidth(16), .bus("separate")) ram_1 (
    .addr(alu_1_aluout), .din(regfile_1_rs_2), .data(ram_1_data), .str(control_1_memw), .clk(Clock_out),
    .ld(control_1_memr), .clr(Reset_out));  // open: sel
  Multiplexer #(.width(16), .enable("false")) multiplexer_5 (
    .in0(alu_1_aluout), .in1(ram_1_data), .out(multiplexer_5_out), .sel(control_1_memtoreg));
endmodule

// Reg
module RegFile (
  input  [2:0] RT,
  input  [15:0] WriteData,
  input  WriteEnable,
  input  [2:0] RS,
  input  Clock,
  output [15:0] RT_2,
  output [15:0] RS_2
);

  wire demultiplexer_1_out0, demultiplexer_1_out1, demultiplexer_1_out2, demultiplexer_1_out3,
       demultiplexer_1_out4, demultiplexer_1_out5, demultiplexer_1_out6, demultiplexer_1_out7;
  wire [15:0] register_1_q, register_2_q, register_3_q, register_4_q, register_5_q, register_6_q,
       register_7_q, register_8_q;

  Demultiplexer #(.select(3), .enable("false")) demultiplexer_1 (
    .out0(demultiplexer_1_out0), .out1(demultiplexer_1_out1), .out2(demultiplexer_1_out2),
    .out3(demultiplexer_1_out3), .out4(demultiplexer_1_out4), .out5(demultiplexer_1_out5),
    .out6(demultiplexer_1_out6), .out7(demultiplexer_1_out7), .in(WriteEnable), .sel(RS));
  Register #(.width(16)) register_1 (
    .D(WriteData), .en(demultiplexer_1_out0), .Q(register_1_q), .clk(Clock));  // open: clr
  Register #(.width(16)) register_2 (
    .D(WriteData), .en(demultiplexer_1_out1), .Q(register_2_q), .clk(Clock));  // open: clr
  Register #(.width(16)) register_3 (
    .D(WriteData), .en(demultiplexer_1_out2), .Q(register_3_q), .clk(Clock));  // open: clr
  Register #(.width(16)) register_4 (
    .D(WriteData), .en(demultiplexer_1_out3), .Q(register_4_q), .clk(Clock));  // open: clr
  Register #(.width(16)) register_5 (
    .D(WriteData), .en(demultiplexer_1_out4), .Q(register_5_q), .clk(Clock));  // open: clr
  Register #(.width(16)) register_6 (
    .D(WriteData), .en(demultiplexer_1_out5), .Q(register_6_q), .clk(Clock));  // open: clr
  Register #(.width(16)) register_7 (
    .D(WriteData), .en(demultiplexer_1_out6), .Q(register_7_q), .clk(Clock));  // open: clr
  Register #(.width(16)) register_8 (
    .D(WriteData), .en(demultiplexer_1_out7), .Q(register_8_q), .clk(Clock));  // open: clr
  Multiplexer #(.select(3), .width(16), .enable("false")) multiplexer_1 (
    .in0(register_1_q), .in1(register_2_q), .in2(register_3_q), .in3(register_4_q), .in4(register_5_q),
    .in5(register_6_q), .in6(register_7_q), .in7(register_8_q), .out(RT_2), .sel(RT));
  Multiplexer #(.select(3), .width(16), .enable("false")) multiplexer_2 (
    .in0(register_1_q), .in1(register_2_q), .in2(register_3_q), .in3(register_4_q), .in4(register_5_q),
    .in5(register_6_q), .in6(register_7_q), .in7(register_8_q), .out(RS_2), .sel(RS));
endmodule

// De
module Decoder (
  input  [15:0] Inst,
  output [3:0] OPcode,
  output [2:0] RT,
  output [2:0] RS,
  output [8:0] Imm,
  output SubOP
);


  assign Imm = Inst[8:0];
  assign OPcode = Inst[15:12];
  assign RS = Inst[11:9];
  assign RT = Inst[8:6];
  assign SubOP = Inst[0];
endmodule

module ALU (
  input  SUBOP,
  input  [15:0] RS,
  input  [15:0] RT_IMM,
  input  [2:0] ALUOP,
  output [15:0] ALUout
);

  wire [15:0] adder_1_out, adder_2_out, adder_3_out, adder_4_out, and_1_out, and_2_out, and_3_out,
       multiplexer_1_out, multiplexer_2_out, multiplexer_3_out, multiplexer_4_out, multiplexer_5_out,
       not_1_out, not_2_out, not_3_out, shifter_1_out, shifter_2_out, shifter_3_out, shifter_4_out;

  assign not_1_out = ~RT_IMM;  // NOT_Gate not_1, 16 bits wide
  assign not_2_out = ~RS;  // NOT_Gate not_2, 16 bits wide
  assign not_3_out = ~RT_IMM;  // NOT_Gate not_3, 16 bits wide
  Shifter #(.width(16)) shifter_1 (.in(RS), .\dist (RT_IMM[3:0]), .out(shifter_1_out));
  Shifter #(.width(16), .shift("lr")) shifter_2 (.in(RS), .\dist (RT_IMM[3:0]), .out(shifter_2_out));
  Shifter #(.width(16)) shifter_3 (.in(RS), .\dist (RT_IMM[4:1]), .out(shifter_3_out));
  Shifter #(.width(16), .shift("lr")) shifter_4 (.in(RS), .\dist (RT_IMM[4:1]), .out(shifter_4_out));
  Multiplexer #(.width(16), .enable("false")) multiplexer_1 (
    .in0(RT_IMM), .in1(adder_1_out), .out(multiplexer_1_out), .sel(SUBOP));
  Adder #(.width(16)) adder_1 (.a(not_1_out), .b(16'h1), .out(adder_1_out));  // open: cin, cout
  assign and_1_out = RS & 16'hff;  // AND_Gate and_1, 16 bits wide
  assign and_2_out = 16'hff & RT_IMM;  // AND_Gate and_2, 16 bits wide
  Multiplexer #(.width(16), .enable("false")) multiplexer_2 (
    .in0(not_2_out), .in1(RS), .out(multiplexer_2_out), .sel(SUBOP));
  assign and_3_out = multiplexer_2_out & multiplexer_3_out;  // AND_Gate and_3, 16 bits wide
  Multiplexer #(.width(16), .enable("false")) multiplexer_3 (
    .in0(not_3_out), .in1(RT_IMM), .out(multiplexer_3_out), .sel(SUBOP));
  Adder #(.width(16)) adder_2 (.a(RS), .b(RT_IMM), .out(adder_2_out));  // open: cin, cout
  Adder #(.width(16)) adder_3 (.a(and_1_out), .b(and_2_out), .out(adder_3_out));  // open: cin, cout
  Multiplexer #(.width(16), .enable("false")) multiplexer_4 (
    .in0(shifter_1_out), .in1(shifter_2_out), .out(multiplexer_4_out), .sel(SUBOP));
  Multiplexer #(.width(16), .enable("false")) multiplexer_5 (
    .in0(shifter_3_out), .in1(shifter_4_out), .out(multiplexer_5_out), .sel(SUBOP));
  Adder #(.width(16)) adder_4 (.a(RS), .b(multiplexer_1_out), .out(adder_4_out));  // open: cin, cout
  Multiplexer #(.select(3), .width(16), .enable("false")) multiplexer_6 (
    .in0(adder_4_out), .in1(adder_2_out), .in2(adder_3_out), .in3(and_3_out), .in4(multiplexer_4_out),
    .in5(multiplexer_5_out), .in7(RT_IMM), .out(ALUout), .sel(ALUOP));  // open: in6
endmodule

// CTL
module Control (
  input  [3:0] OP,
  input  SubOP,
  output RegWrite,
  output ALUsrc,
  output [2:0] ALUop,
  output MemR,
  output MemW,
  output MemToReg,
  output PCtoReg,
  output HexW,
  output ProgEn,
  output JR,
  output [2:0] BranchOP
);

  wire and_1_out, and_4_out, and_5_out, and_6_out, and_7_out, and_8_out, and_9_out, and_14_out, and_15_out,
       and_16_out, and_17_out, and_18_out, not_1_out, not_2_out, not_3_out, not_4_out, not_5_out, not_6_out,
       not_7_out, not_8_out, not_9_out, not_10_out, not_11_out, not_12_out, not_13_out, not_14_out,
       not_15_out, not_16_out, not_17_out, not_18_out, not_19_out, not_20_out, not_21_out, not_22_out,
       not_23_out, not_24_out, not_25_out, not_26_out, not_27_out, not_28_out;

  not not_1 (not_1_out, OP[3]);
  not not_2 (not_2_out, OP[2]);
  not not_3 (not_3_out, OP[3]);
  not not_4 (not_4_out, OP[1]);
  not not_5 (not_5_out, OP[3]);
  not not_6 (not_6_out, OP[0]);
  not not_7 (not_7_out, SubOP);
  not not_8 (not_8_out, OP[1]);
  not not_9 (not_9_out, OP[0]);
  not not_10 (not_10_out, OP[1]);
  not not_11 (not_11_out, OP[2]);
  not not_12 (not_12_out, OP[0]);
  and and_1 (and_1_out, OP[2], OP[1]);
  not not_13 (not_13_out, SubOP);
  not not_14 (not_14_out, OP[3]);
  not not_15 (not_15_out, OP[0]);
  and and_2 (MemToReg, OP[2], OP[1]);
  not not_16 (not_16_out, OP[1]);
  not not_17 (not_17_out, OP[0]);
  and and_3 (HexW, OP[3], OP[2], OP[1], OP[0]);
  not not_18 (not_18_out, OP[2]);
  not not_19 (not_19_out, OP[1]);
  not not_20 (not_20_out, OP[0]);
  not not_21 (not_21_out, OP[1]);
  not not_22 (not_22_out, OP[2]);
  not not_23 (not_23_out, OP[0]);
  not not_24 (not_24_out, OP[2]);
  not not_25 (not_25_out, OP[1]);
  not not_26 (not_26_out, OP[0]);
  not not_27 (not_27_out, OP[0]);
  not not_28 (not_28_out, OP[0]);
  and and_4 (and_4_out, not_1_out, not_2_out);
  and and_5 (and_5_out, not_3_out, not_4_out);
  and and_6 (and_6_out, not_5_out, not_6_out, not_7_out);
  and and_7 (and_7_out, OP[2], not_8_out, not_9_out);
  and and_8 (and_8_out, not_10_out, OP[0]);
  and and_9 (and_9_out, not_11_out, OP[1], not_12_out);
  or or_1 (ALUop[0], OP[0], and_1_out);
  and and_10 (MemR, OP[2], OP[1], not_13_out);
  and and_11 (MemW, not_14_out, OP[2], OP[1], not_15_out, SubOP);
  and and_12 (PCtoReg, OP[3], not_16_out, not_17_out);
  or or_2 (ProgEn, not_18_out, not_19_out, not_20_out, OP[3]);
  and and_13 (JR, OP[3], OP[2], not_21_out, OP[0]);
  and and_14 (and_14_out, OP[3], not_22_out, OP[1], OP[0]);
  and and_15 (and_15_out, OP[3], OP[2], not_23_out);
  and and_16 (and_16_out, OP[3], not_24_out, not_25_out, OP[0]);
  and and_17 (and_17_out, OP[3], OP[1], not_26_out);
  and and_18 (and_18_out, OP[3], OP[2], not_27_out);
  and and_19 (BranchOP[0], OP[3], not_28_out);
  or or_3 (RegWrite, and_4_out, and_5_out, and_6_out, and_7_out);
  or or_4 (ALUsrc, and_8_out, and_9_out);
  or or_5 (BranchOP[2], and_14_out, and_15_out);
  or or_6 (BranchOP[1], and_16_out, and_17_out, and_18_out);

  assign ALUop[2:1] = OP[2:1];
endmodule

// Br
module Branch (
  input  [15:0] RS,
  input  [2:0] BranchOp,
  output Branch
);

  wire not_1_out, not_2_out, or_1_out;

  or or_1 (or_1_out, RS[0], RS[1], RS[2], RS[3], RS[4], RS[5], RS[6], RS[7], RS[8], RS[9], RS[10], RS[11], RS[12], RS[13], RS[14], RS[15]);
  not not_1 (not_1_out, RS[15]);
  not not_2 (not_2_out, or_1_out);
  Multiplexer #(.select(3), .enable("false")) multiplexer_1 (
    .in0(1'b0), .in1(not_2_out), .in2(or_1_out), .in3(not_1_out), .in4(RS[15]), .in7(1'b1), .out(Branch),
    .sel(BranchOp));  // open: in5, in6
endmodule

// Extd
module Signing (
  input  [8:0] Sign___Imm,
  output [15:0] Imm_Value
);

  wire [15:0] bit_extender_1_out, bit_extender_2_out;

  assign bit_extender_1_out = {{8{1'b0}}, Sign___Imm[7:0]};  // Bit_Extender bit_extender_1
  assign bit_extender_2_out = {{8{Sign___Imm[7]}}, Sign___Imm[7:0]};  // Bit_Extender bit_extender_2
  Multiplexer #(.width(16), .enable("false")) multiplexer_1 (
    .in0(bit_extender_1_out), .in1(bit_extender_2_out), .out(Imm_Value), .sel(Sign___Imm[8]));
endmodule
